# Fritzing sketch LightFunNoPCB (saved by Fritzing 0.9.0b)

parts:
  Part2 = Arduino Pro Mini v13
  TIP31C = npn-Powertransistor [package="TO220 [THT]"]
  TIP31C1 = npn-Powertransistor [package="TO220 [THT]"]
  R2 = Resistor [tolerance=±5% resistance=470 package=THT]
  R1 = Resistor [tolerance=±5% resistance=470 package=THT]
  TIP31C2 = npn-Powertransistor [package="TO220 [THT]"]
  R3 = Resistor [tolerance=±5% resistance=470 package=THT]
  Part3 = FTDI Basic Programmer
  JACK1 = 2.1mm Barrel Jack with Terminal Block
  C1 = Ceramic Capacitor [capacitance=100nF voltage=16V package="1206 [SMD, multilayer]"]
  Part4 = Breakout Board for Electret Microphone
  R4 = Resistor [tolerance=±5% resistance=220 package=THT]

nets:
  N1: Part2.D0/TX, Part3.RXI
  N2: Part2.D1/RX, Part3.TXO
  N3: Part2.VCC, Part3.POWER
  GND: Part2.GND, TIP31C.emitter, TIP31C1.emitter, TIP31C2.emitter, Part3.GND, JACK1.NEG, C1.0, Part4.GND
  N4: Part2.RAW, JACK1.POS, Part4.VCC
  N5: Part2.A0, C1.1, R4.Pin_1
  N6: Part2.D9_PWM, R3.Pin_1
  N7: Part2.D5_PWM, R2.Pin_1
  N8: Part2.D3_PWM, R1.Pin_1
  N9: TIP31C.base, R2.Pin_0
  N10: TIP31C1.base, R1.Pin_0
  N11: TIP31C2.base, R3.Pin_0
  N12: Part4.AUD, R4.Pin_0

notes:
  TO LED STRIP
